# Fritzing sketch Circuit_Diagram (saved by Fritzing 0.9.3b)

parts:
  U2 = ESP32S-HiLetgo [part_number=ESP32S-HiLetgo]
  U5 = LCD-16X2 [package=lcd-16x2_noholes]
  LCM1602_IIC1 = LCM1602 IIC [part_number="LCM1602 IIC" chip_label="LCM1602 IIC" package="DIP (Dual Inline) [THT]"]
  U6 = 2-Channel 5v Relay Shield [package=relay-2ch5v10a]
  M1 = DC Motor
  BULB2 = Incandescent light bulb small [package="bulb sm"]

nets:
  N1: U2.GPIO26, U6.IN2
  N2: U2.GPIO2, U6.IN1
  N3: U2.GPIO21, LCM1602_IIC1.SCL
  N4: U2.GPIO22, LCM1602_IIC1.SDA
  GND: U2.GND, LCM1602_IIC1.GND
  N5: U5.VSS, LCM1602_IIC1.K
  N6: U5.VDD, LCM1602_IIC1.A
  N7: U5.VO, LCM1602_IIC1.D7
  N8: U5.RS, LCM1602_IIC1.D6
  N9: U5.R_W, LCM1602_IIC1.D5
  N10: U5.E, LCM1602_IIC1.D4
  N11: U5.DB0, LCM1602_IIC1.D3
  N12: U5.DB1, LCM1602_IIC1.D2
  N13: U5.DB2, LCM1602_IIC1.D1
  N14: U5.DB3, LCM1602_IIC1.D0
  N15: U5.DB4, LCM1602_IIC1.E
  N16: U5.DB5, LCM1602_IIC1.RW
  N17: U5.DB6, LCM1602_IIC1.RS
  N18: U5.DB7, LCM1602_IIC1.V0
  N19: U5.A, LCM1602_IIC1.VDD
  N20: U5.K, LCM1602_IIC1.VSS
  N21: U6.K1-On, BULB2.2
  N22: U6.K2-On, M1.pin_2

notes:
  +5V
  220V AC

custom parts:
  ESP32S-HiLetgo: HiLetgo ESP-WROOM-32 ESP32 ESP-32S Development Board 2.4GHz Dual-Mode WiFi + Bluetooth Dual Cores Microcontroller The ESP32 integrated with Antenna switches, RF Balun, power amplifiers, low-noise amplifiers, filters, and management modules, and the entire solution occupies the least area of PCB. 2.4 GHz Wi-Fi plus Bluetooth dual-mode chip, with TSMC Ultra-low power consumption 40nm technology,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
  LCM1602 IIC: I2C-Module to use a 1602 or 2004 LCD on with the wire.h libory Serial LCD Modul
  2-Channel 5v Relay Shield: 2 Channel 5v Relay Shield w. 2x SPD-06VDC-SD-C
